// Logisim project 重定向.circ as structural Verilog: 19 circuits, main circuit main
module main (
);

  wire AluB, and_1_out, and_2_out, bat, branch, clk, DMWrite, equal, halt, id_ex_1_rs_r_, id_ex_1_rt_r_, j,
       jal5, jal_EX, jal_MEM, not_1_out, not_2_out, not_4_out, or_1_out, or_2_out, PopJumpRst, PopSignal,
       RegDin5, RegDinEx, RegDinMem, RegDst5, RegDST_EX, RegDST_MEM, RegW5, RegWrite_EX, RegWrite_MEM, ret,
       RS_R, rst, RT_R, sel1, sel2, sel3, sel4, sys, sys3, UnLoadUseSignal;
  wire [1:0] sft, sft3;
  wire [3:0] aluop, mode, multiplexer_19_out, not_3_out, or_3_out, registerfile_1_p9, \操作控制器_1_aluop ,
       \操作控制器_1_mode ;
  wire [4:0] and_3_out, ex_mem_1_rs_, id_ex_1_rd_, multiplexer_3_out, multiplexer_5_out, multiplexer_7_out,
       multiplexer_8_out, multiplexer_9_out, multiplexer_10_out, multiplexer_18_out, rA, rB, rd5, RD_MEM,
       RS_EX, rt5, RT_EX, RT_MEM, \指令解析器ir_1_rd , \指令解析器ir_1_rs , \指令解析器ir_1_rt ;
  wire [5:0] \指令解析器ir_1_func , \指令解析器ir_1_op ;
  wire [9:3] id_ex_1_ctrl_;
  wire [10:0] \操作控制器_1_jump ;
  wire [15:0] pop_count, \总周期数 , \无条件分支指令数 , \有条件分支成功跳转 , \有条件分支指令数 ;
  wire [22:0] ex_mem_1_ctrl_, mem_wb_1_ctrl_;
  wire [25:0] id_ex_1_ins26_2, \指令解析器ir_1_ins26 ;
  wire [31:0] adder_1_out, ALUR_Mem, ALUR_Wb, DMOut, ex_mem_1_pc_4, ex_mem_1_reg_2, id_ex_1_ins16_32_,
       id_ex_1_instant, id_ex_1_pc_4, id_ex_1_reg_1, id_ex_1_reg_2, \if_id锁存_1_pc_4 , \if_id锁存_1_输出指令 ,
       l_alu_004cea74_1_p5, mem_wb_1_pc_4, mips_ram_1_p7, multiplexer_1_out, multiplexer_11_out,
       multiplexer_12_out, multiplexer_13_out, multiplexer_14_out, multiplexer_15_out, multiplexer_16_out,
       multiplexer_17_out, npc_1_pcout, PC_q, registerfile_1_p7, registerfile_1_p8, RegWriteWB, rom_1_data,
       shifter_1_out, SyscallOut, \指令解析器ir_1_ins , \指令解析器ir_1_ins16_32 ;

  and and_1 (and_1_out, not_1_out, halt);
  Button \u_总复位  (.out(rst));
  Register #(.width(32)) PC (.D(npc_1_pcout), .en(and_1_out), .Q(PC_q), .clk(clk), .clr(rst));
  not not_1 (not_1_out, PopSignal);
  Hex_Digit_Display hex_digit_display_1 (.value(SyscallOut[31:28]));  // open: dp
  Adder #(.width(32)) adder_1 (.a(PC_q), .b(32'h4), .out(adder_1_out));  // open: cin, cout
  NPC npc_1 (
    .pc_4(adder_1_out), .imm26(id_ex_1_ins26_2), ._16_32(id_ex_1_ins16_32_), .reg1(multiplexer_13_out),
    .pcout(npc_1_pcout), .jump(j), .branch(branch), .\return (ret), .PC4(id_ex_1_pc_4));
  Hex_Digit_Display hex_digit_display_2 (.value(SyscallOut[23:20]));  // open: dp
  Hex_Digit_Display hex_digit_display_3 (.value(SyscallOut[27:24]));  // open: dp
  Hex_Digit_Display hex_digit_display_4 (.value(SyscallOut[15:12]));  // open: dp
  Hex_Digit_Display hex_digit_display_5 (.value(SyscallOut[19:16]));  // open: dp
  \IF_ID锁存  \if_id锁存_1  (
    .\指令 (rom_1_data), .\输出指令 (\if_id锁存_1_输出指令 ), .clk(clk), .rst(or_1_out), .pc4(adder_1_out),
    .pc_4(\if_id锁存_1_pc_4 ), .halt(and_2_out));
  ROM #(.addrWidth(10), .dataWidth(32)) rom_1 (.addr(PC_q[11:2]), .data(rom_1_data));  // open: sel
  or or_1 (or_1_out, PopJumpRst, rst);
  Hex_Digit_Display hex_digit_display_6 (.value(SyscallOut[7:4]));  // open: dp
  Hex_Digit_Display hex_digit_display_7 (.value(SyscallOut[11:8]));  // open: dp
  \操作控制器  \u_操作控制器_1  (
    .op(\指令解析器ir_1_op ), .jump(\操作控制器_1_jump [0]), .\return (\操作控制器_1_jump [2]), .JAL(\操作控制器_1_jump [1]),
    .RegDin(\操作控制器_1_jump [7]), .func(\指令解析器ir_1_func ), .shift(sft), .ALUOP(\操作控制器_1_aluop ), .sys(sys),
    .RegWrite(\操作控制器_1_jump [8]), .DMWrite(\操作控制器_1_jump [9]), .mode(\操作控制器_1_mode ),
    .AluB(\操作控制器_1_jump [10]), .RegDst(\操作控制器_1_jump [6]), .beq(\操作控制器_1_jump [3]), .bne(\操作控制器_1_jump [4]),
    .blez(\操作控制器_1_jump [5]), .RS_R(RS_R), .RT_R(RT_R));
  \指令解析器IR  \u_指令解析器ir_1  (
    .op(\指令解析器ir_1_op ), .func(\指令解析器ir_1_func ), .\输入指令 (\if_id锁存_1_输出指令 ), .rs(\指令解析器ir_1_rs ),
    .ins16_32(\指令解析器ir_1_ins16_32 ), .rt(\指令解析器ir_1_rt ), .rd(\指令解析器ir_1_rd ), .ins26(\指令解析器ir_1_ins26 ),
    .shift(sft), .ins(\指令解析器ir_1_ins ));
  and and_2 (and_2_out, not_2_out, halt);
  Hex_Digit_Display hex_digit_display_8 (.value(SyscallOut[3:0]));  // open: dp
  not not_2 (not_2_out, PopSignal);
  // Probe on \总周期数 
  // Probe on \无条件分支指令数 
  // Probe on \有条件分支指令数 
  // Probe on \有条件分支成功跳转 
  // Probe on pop_count
  \气泡检测  \u_气泡检测_1  (
    .RA(rA), .Bub_Signal(PopSignal), .RT_EX(RT_EX), .RS_EX(id_ex_1_rd_), .Jump_RESET(PopJumpRst),
    .reg_EX(RegDST_EX), .jal_EX(jal_EX), .J(j), .Branch(branch), .Ret(ret), .RB(rB), .RS_R(RS_R),
    .RT_R(RT_R), .RegDinEx(RegDinEx), .UN_LoadUseSignal(UnLoadUseSignal), .RegWriteEX(RegWrite_EX));
  Multiplexer #(.width(32), .enable("false")) multiplexer_1 (
    .in0(ALUR_Wb), .in1(DMOut), .out(multiplexer_1_out), .sel(RegDin5));
  Multiplexer #(.width(32), .enable("false")) multiplexer_2 (
    .in0(multiplexer_1_out), .in1(mem_wb_1_pc_4), .out(RegWriteWB), .sel(jal5));
  Multiplexer #(.width(5), .enable("false")) multiplexer_3 (
    .in0(multiplexer_5_out), .in1({5{1'b1}}), .out(multiplexer_3_out), .sel(jal5));
  Multiplexer #(.width(5), .enable("false")) multiplexer_4 (.in0(\指令解析器ir_1_rs ), .in1(5'b00010), .out(rA), .sel(sys));
  Multiplexer #(.width(5), .enable("false")) multiplexer_5 (
    .in0(rd5), .in1(rt5), .out(multiplexer_5_out), .sel(RegDst5));
  \计数器  \u_计数器_1  (
    .clk(clk), .branch(branch), .jump(j), .\总周期 (\总周期数 ), .RST(rst), .bat(bat), .\return (ret),
    .\无条件 (\无条件分支指令数 ), .\有条件 (\有条件分支指令数 ), .halt(halt), .\有条件成功 (\有条件分支成功跳转 ), .pop_2(pop_count),
    .pop(PopSignal));
  // RegisterFile registerfile_1: pin names not known; wires that end beside it: RegWriteWB, clk, RegW5, multiplexer_3_out, rA, rB, registerfile_1_p7, registerfile_1_p8, registerfile_1_p9
  Multiplexer #(.width(5), .enable("false")) multiplexer_6 (.in0(\指令解析器ir_1_rt ), .in1(5'b00100), .out(rB), .sel(sys));
  or or_2 (or_2_out, rst, PopSignal, PopJumpRst);
  Multiplexer #(.width(5), .enable("false")) multiplexer_7 (
    .in0(multiplexer_8_out), .in1({5{1'b1}}), .out(multiplexer_7_out), .sel(jal5));
  Multiplexer #(.width(5), .enable("false")) multiplexer_8 (
    .in0(rd5), .in1(rt5), .out(multiplexer_8_out), .sel(RegDst5));
  ID_EX id_ex_1 (
    .reg1(registerfile_1_p7), .reg2(registerfile_1_p8), .ins(\指令解析器ir_1_ins ), .clk(clk),
    .reg_1(id_ex_1_reg_1), .reg_2(id_ex_1_reg_2), .instant(id_ex_1_instant), .pc4(\if_id锁存_1_pc_4 ),
    .pc_4(id_ex_1_pc_4), .ctrl({\操作控制器_1_aluop , \操作控制器_1_mode , sys, sft, \操作控制器_1_jump }),
    .ctrl_({aluop, registerfile_1_p9, sys3, sft3, AluB, id_ex_1_ctrl_[9], RegWrite_EX, RegDinEx, RegDST_EX, id_ex_1_ctrl_[5:3], ret, jal_EX, j}),
    .rs(\指令解析器ir_1_rs ), .rt(\指令解析器ir_1_rt ), .rs_(RS_EX), .rt_(RT_EX), .halt(halt), .Bub_Signal(or_2_out),
    .ins26(\指令解析器ir_1_ins26 ), .ins16_32(\指令解析器ir_1_ins16_32 ), .ins16_32_(id_ex_1_ins16_32_),
    .ins26_2(id_ex_1_ins26_2), .rd(\指令解析器ir_1_rd ), .rd_(id_ex_1_rd_), .Rt_R(RT_R), .RS_R(RS_R),
    .RT_R_(id_ex_1_rt_r_), .RS_R_(id_ex_1_rs_r_));
  \重定向  \u_重定向_1  (
    .RS_EX(RS_EX), .rs_r(id_ex_1_rs_r_), .RT_EX(RT_EX), .rt_r(id_ex_1_rt_r_), .rw4(multiplexer_9_out),
    .rw5(multiplexer_7_out), .regWrite4(RegWrite_MEM), .regWrite5(RegW5), .sel1(sel1), .sel2(sel2),
    .RegDin4(RegDinMem), .sel3(sel3), .sel4(sel4), .jal4(jal_MEM), .Sys_EX(sys3));
  Multiplexer #(.width(5), .enable("false")) multiplexer_9 (
    .in0(multiplexer_10_out), .in1({5{1'b1}}), .out(multiplexer_9_out), .sel(jal_MEM));
  Multiplexer #(.width(5), .enable("false")) multiplexer_10 (
    .in0(RD_MEM), .in1(RT_MEM), .out(multiplexer_10_out), .sel(RegDST_MEM));
  Multiplexer #(.width(32), .enable("false")) multiplexer_11 (
    .in0(id_ex_1_reg_1), .in1(RegWriteWB), .out(multiplexer_11_out), .sel(sel3));
  Multiplexer #(.width(32), .enable("false")) multiplexer_12 (
    .in0(id_ex_1_reg_2), .in1(RegWriteWB), .out(multiplexer_12_out), .sel(sel4));
  Multiplexer #(.width(32), .enable("false")) multiplexer_13 (
    .in0(multiplexer_11_out), .in1(ALUR_Mem), .out(multiplexer_13_out), .sel(sel1));
  Multiplexer #(.width(32), .enable("false")) multiplexer_14 (
    .in0(multiplexer_12_out), .in1(ALUR_Mem), .out(multiplexer_14_out), .sel(sel2));
  Multiplexer #(.select(2), .width(32), .enable("false")) multiplexer_15 (
    .in0(multiplexer_13_out), .in1(multiplexer_14_out), .out(multiplexer_15_out), .sel(sft3));  // open: in2, in3
  Multiplexer #(.width(32), .enable("false")) multiplexer_16 (
    .in0(multiplexer_14_out), .in1(id_ex_1_instant), .out(multiplexer_16_out), .sel(AluB));
  Multiplexer #(.width(32), .enable("false")) multiplexer_17 (
    .in0(multiplexer_16_out), .in1(32'ha), .out(multiplexer_17_out), .sel(sys3));
  branch_halt branch_halt_1 (
    .beq(id_ex_1_ctrl_[3]), .branch(branch), .bat(bat), .bne(id_ex_1_ctrl_[4]), .blez(id_ex_1_ctrl_[5]),
    .in_5(equal), .syscall(sys3), .alur(l_alu_004cea74_1_p5));
  // L_ALU_004cea74 l_alu_004cea74_1: pin names not known; wires that end beside it: multiplexer_15_out, multiplexer_17_out, aluop, equal, l_alu_004cea74_1_p5
  EX_MEM ex_mem_1 (
    .aluR(l_alu_004cea74_1_p5), .reg2(multiplexer_14_out), .clk(clk), .rst(rst), .alu_R(ALUR_Mem),
    .reg_2(ex_mem_1_reg_2), .pc4(id_ex_1_pc_4), .pc_4(ex_mem_1_pc_4),
    .ctrl({equal, aluop, registerfile_1_p9, sys3, sft3, AluB, id_ex_1_ctrl_[9], RegWrite_EX, RegDinEx, RegDST_EX, id_ex_1_ctrl_[5:3], ret, jal_EX, j}),
    .ctrl_({ex_mem_1_ctrl_[22:18], mode, ex_mem_1_ctrl_[13:10], DMWrite, RegWrite_MEM, RegDinMem, RegDST_MEM, ex_mem_1_ctrl_[5:2], jal_MEM, ex_mem_1_ctrl_[0]}),
    .rs(RS_EX), .rt(RT_EX), .rs_(ex_mem_1_rs_), .rt_(RT_MEM), .halt(halt), .rd(id_ex_1_rd_), .rd_(RD_MEM));
  Multiplexer #(.select(2), .width(5), .enable("false")) multiplexer_18 (
    .in0({5{1'b0}}), .in1(5'b01000), .in2(5'b10000), .in3(5'b11000), .out(multiplexer_18_out),
    .sel(ALUR_Mem[1:0]));
  assign and_3_out = multiplexer_18_out & {{2{not_3_out[3]}}, not_3_out[2:0]};  // AND_Gate and_3, 5 bits wide
  Shifter #(.width(32)) shifter_1 (.in(ex_mem_1_reg_2), .\dist (and_3_out), .out(shifter_1_out));
  Multiplexer #(.select(2), .width(4), .enable("false")) multiplexer_19 (
    .in0(4'b0001), .in1(4'b0010), .in2(4'b0100), .in3(4'b1000), .out(multiplexer_19_out), .sel(ALUR_Mem[1:0]));
  Clock clock_1 (.out(clk));
  assign not_3_out = ~mode;  // NOT_Gate not_3, 4 bits wide
  not not_4 (not_4_out, clk);
  assign or_3_out = multiplexer_19_out | mode;  // OR_Gate or_3, 4 bits wide
  MEM_WB mem_wb_1 (
    .DMout(mips_ram_1_p7), .clk(clk), .rst(rst), .DM_out(DMOut), .pc4(ex_mem_1_pc_4), .aluR(ALUR_Mem),
    .pc_4(mem_wb_1_pc_4), .alu_R(ALUR_Wb),
    .ctrl({ex_mem_1_ctrl_[22:18], mode, ex_mem_1_ctrl_[13:10], DMWrite, RegWrite_MEM, RegDinMem, RegDST_MEM, ex_mem_1_ctrl_[5:2], jal_MEM, ex_mem_1_ctrl_[0]}),
    .ctrl_({mem_wb_1_ctrl_[22:9], RegW5, RegDin5, RegDst5, mem_wb_1_ctrl_[5:2], jal5, mem_wb_1_ctrl_[0]}),
    .rs(ex_mem_1_rs_), .rt(RT_MEM), .rt_(rt5), .halt(halt), .rd(RD_MEM), .rd_(rd5));  // open: rs_
  // MIPS_RAM mips_ram_1: pin names not known; wires that end beside it: ALUR_Mem[13:2], shifter_1_out, DMWrite, or_3_out, not_4_out, rst, mips_ram_1_p7
  nand nand_1 (halt, mem_wb_1_ctrl_[13], mem_wb_1_ctrl_[22]);
  \显示器  \u_显示器_1  (.syscallout(SyscallOut), .sys(sys3), .clk(clk), .in_3(equal), .rst(rst), .reg2(multiplexer_14_out));

  // Notes on the sheet:
  //   指令存储器IM
  //   contents of rom_1 (hex, n*v repeats v):
  //   20110001 8000c05 20110001 20120002 20130003 8000c09 20110001 20120002 20130003 8000c0d 20110001
  //   20120002 20130003 8000c11 20110001 20120002 20130003 c000cee 20100001 20110001 118fc0 112020
  //   20020022 c 118882 12200001 8000c15 112020 20020022 c 20110001 118880 112020 20020022 c 12200001
  //   8000c1f 20110001 118fc0 112020 20020022 c 1188c3 112020 20020022 c 118903 112020 20020022 c 118903
  //   112020 20020022 c 118903 112020 20020022 c 118903 112020 20020022 c 118903 112020 20020022 c 118903
  //   112020 20020022 c 118903 112020 20020022 c 20100001 109fc0 139fc3 8021 2012000c 24160003 26100001
  //   3210000f 20080008 20090001 139900 2709825 132020 20020022 c 1094022 1500fff9 22100001 2018000f
  //   2188024 108700 20080008 20090001 139902 2709825 132021 20020022 c 1094022 1500fff9 108702 2c9b022
  //   12c00001 8000c50 4020 1084027 84400 3508ffff 82021 20020022 c 2010ffff 20110000 ae300000 22100001
  //   22310004 ae300000 22100001 22310004 ae300000 22100001 22310004 ae300000 22100001 22310004 ae300000
  //   22100001 22310004 ae300000 22100001 22310004 ae300000 22100001 22310004 ae300000 22100001 22310004
  //   ae300000 22100001 22310004 ae300000 22100001 22310004 ae300000 22100001 22310004 ae300000 22100001
  //   22310004 ae300000 22100001 22310004 ae300000 22100001 22310004 ae300000 22100001 22310004 ae300000
  //   22100001 22310004 22100001 8020 2011003c 8e130000 8e340000 274402a 11000002 ae330000 ae140000
  //   2231fffc 1611fff8 102020 20020022 c 22100004 2011003c 1611fff2 20020032 c 2008ffff 20117777 112020
  //   20020022 c 200b0010 2288826 112020 20020022 c 216bffff 1560fffa c 2008ffff 20090000 20111997 112020
  //   20020022 c 2288820 2e291949 1120fffa c 20090000 200b0020 20110000 20120001 a1310000 112020 20020022
  //   c 2328820 21290001 216bffff 1560fff8 200b0008 20090000 8d310000 112020 20020022 c 21290004 216bffff
  //   1560fff9 c 2011fff1 112020 20020022 c 22310001 1a20fffb c 2002000a c 20100000 22100001 102020
  //   20020022 c 22100002 102020 20020022 c 22100003 102020 20020022 c 22100004 102020 20020022 c 22100005
  //   102020 20020022 c 22100006 102020 20020022 c 22100007 102020 20020022 c 22100008 102020 20020022
  //   20020022 c 3e00008
endmodule

module \指令解析  (
  input  [31:0] \输入指令 ,
  output [5:0] out_2,
  output [4:0] out_3,
  output [4:0] out_4,
  output [4:0] out_5,
  output [4:0] out_6,
  output [5:0] out_7,
  output [15:0] out_8,
  output [25:0] out_9
);


  assign out_2 = \输入指令 [31:26];
  assign out_3 = \输入指令 [25:21];
  assign out_4 = \输入指令 [20:16];
  assign out_5 = \输入指令 [15:11];
  assign out_6 = \输入指令 [10:6];
  assign out_7 = \输入指令 [5:0];
  assign out_8 = \输入指令 [15:0];
  assign out_9 = \输入指令 [25:0];

  // Other names for the same wires on the sheet: func[5:0] = \输入指令 [5:0]; ins16[15:0] = \输入指令 [15:0];
  //   ins26[25:0] = \输入指令 [25:0]; 输入[31:0] = \输入指令 ; shamt[4:0] = \输入指令 [10:6]; rd[4:0] = \输入指令 [15:11];
  //   rt[4:0] = \输入指令 [20:16]; rs[4:0] = \输入指令 [25:21]; op[5:0] = \输入指令 [31:26]
endmodule

module \操作控制器  (
  input  [5:0] op,
  input  [5:0] func,
  output jump,
  output JAL,
  output \return ,
  output beq,
  output bne,
  output blez,
  output RegDst,
  output RegDin,
  output RegWrite,
  output DMWrite,
  output AluB,
  output [1:0] shift,
  output sys,
  output [3:0] mode,
  output [3:0] ALUOP,
  output RS_R,
  output RT_R
);

  wire add, addi, addiu, addu, \and , and_14_out, andi, comparator_16_eq, comparator_17_eq, comparator_18_eq,
       comparator_19_eq, comparator_20_eq, comparator_21_eq, comparator_22_eq, comparator_23_eq,
       comparator_24_eq, comparator_25_eq, comparator_26_eq, comparator_27_eq, comparator_28_eq, inst1,
       inst2, inst3, j, \nor , nor_1_out, not_1_out, \or , or_1_out, or_2_out, or_3_out, or_4_out, or_5_out,
       or_6_out, or_11_out, or_17_out, ori, r, SB, sll, slt, slti, sltiu, sltu, sra, srl, sub, sw, \xor ;

  Comparator #(.width(6)) comparator_1 (.a(op), .b({6{1'b0}}), .eq(r));  // open: gt, lt
  Comparator #(.width(6)) comparator_2 (.a(op), .b(6'b001000), .eq(addi));  // open: gt, lt
  Comparator #(.width(6)) comparator_3 (.a(op), .b(6'b001001), .eq(addiu));  // open: gt, lt
  Comparator #(.width(6)) comparator_4 (.a(op), .b(6'b001100), .eq(andi));  // open: gt, lt
  Comparator #(.width(6)) comparator_5 (.a(op), .b(6'b001101), .eq(ori));  // open: gt, lt
  Comparator #(.width(6)) comparator_6 (.a(op), .b(6'b001010), .eq(slti));  // open: gt, lt
  Comparator #(.width(6)) comparator_7 (.a(op), .b(6'b001011), .eq(sltiu));  // open: gt, lt
  Comparator #(.width(6)) comparator_8 (.a(op), .b(6'b100011), .eq(RegDin));  // open: gt, lt
  Comparator #(.width(6)) comparator_9 (.a(op), .b(6'b101011), .eq(sw));  // open: gt, lt
  Comparator #(.width(6)) comparator_10 (.a(op), .b(6'b101000), .eq(SB));  // open: gt, lt
  Comparator #(.width(6)) comparator_11 (.a(op), .b(6'b000100), .eq(beq));  // open: gt, lt
  Comparator #(.width(6)) comparator_12 (.a(op), .b(6'b000101), .eq(bne));  // open: gt, lt
  Comparator #(.width(6)) comparator_13 (.a(op), .b(6'b000110), .eq(blez));  // open: gt, lt
  Comparator #(.width(6)) comparator_14 (.a(op), .b(6'b000010), .eq(j));  // open: gt, lt
  Comparator #(.width(6)) comparator_15 (.a(op), .b(6'b000011), .eq(JAL));  // open: gt, lt
  Comparator #(.width(6)) comparator_16 (.a(func), .b(6'b100000), .eq(comparator_16_eq));  // open: gt, lt
  Comparator #(.width(6)) comparator_17 (.a(func), .b(6'b100001), .eq(comparator_17_eq));  // open: gt, lt
  Comparator #(.width(6)) comparator_18 (.a(func), .b(6'b100100), .eq(comparator_18_eq));  // open: gt, lt
  Comparator #(.width(6)) comparator_19 (.a(func), .b({6{1'b0}}), .eq(comparator_19_eq));  // open: gt, lt
  Comparator #(.width(6)) comparator_20 (.a(func), .b(6'b000011), .eq(comparator_20_eq));  // open: gt, lt
  Comparator #(.width(6)) comparator_21 (.a(func), .b(6'b000010), .eq(comparator_21_eq));  // open: gt, lt
  Comparator #(.width(6)) comparator_22 (.a(func), .b(6'b100010), .eq(comparator_22_eq));  // open: gt, lt
  Comparator #(.width(6)) comparator_23 (.a(func), .b(6'b100101), .eq(comparator_23_eq));  // open: gt, lt
  Comparator #(.width(6)) comparator_24 (.a(func), .b(6'b100111), .eq(comparator_24_eq));  // open: gt, lt
  Comparator #(.width(6)) comparator_25 (.a(func), .b(6'b101010), .eq(comparator_25_eq));  // open: gt, lt
  Comparator #(.width(6)) comparator_26 (.a(func), .b(6'b101011), .eq(comparator_26_eq));  // open: gt, lt
  Comparator #(.width(6)) comparator_27 (.a(func), .b(6'b001000), .eq(comparator_27_eq));  // open: gt, lt
  Comparator #(.width(6)) comparator_28 (.a(func), .b(6'b001100), .eq(comparator_28_eq));  // open: gt, lt
  Comparator #(.width(6)) comparator_29 (.a(func), .b(6'b100110), .eq(\xor ));  // open: gt, lt
  and and_1 (add, r, comparator_16_eq);
  and and_2 (addu, r, comparator_17_eq);
  and and_3 (\and , r, comparator_18_eq);
  and and_4 (sll, r, comparator_19_eq);
  and and_5 (sra, r, comparator_20_eq);
  and and_6 (srl, r, comparator_21_eq);
  and and_7 (sub, r, comparator_22_eq);
  and and_8 (\or , r, comparator_23_eq);
  and and_9 (\nor , r, comparator_24_eq);
  and and_10 (slt, r, comparator_25_eq);
  and and_11 (sltu, r, comparator_26_eq);
  and and_12 (\return , r, comparator_27_eq);
  and and_13 (sys, r, comparator_28_eq);
  assign ALUOP = sll ? 4'b0000 : 4'bz;  // Controlled_Buffer controlled_buffer_1
  assign ALUOP = sra ? 4'b0001 : 4'bz;  // Controlled_Buffer controlled_buffer_2
  assign ALUOP = srl ? 4'b0010 : 4'bz;  // Controlled_Buffer controlled_buffer_3
  assign ALUOP = or_1_out ? 4'b0101 : 4'bz;  // Controlled_Buffer controlled_buffer_4
  or or_1 (or_1_out, add, RegDin, addi, SB, addiu, sw, addu);
  assign ALUOP = sub ? 4'b0110 : 4'bz;  // Controlled_Buffer controlled_buffer_5
  assign ALUOP = or_2_out ? 4'b0111 : 4'bz;  // Controlled_Buffer controlled_buffer_6
  or or_2 (or_2_out, \and , andi);
  assign ALUOP = or_3_out ? 4'b1000 : 4'bz;  // Controlled_Buffer controlled_buffer_7
  or or_3 (or_3_out, \or , ori);
  assign ALUOP = \xor  ? 4'b1001 : 4'bz;  // Controlled_Buffer controlled_buffer_8
  assign ALUOP = \nor  ? 4'b1010 : 4'bz;  // Controlled_Buffer controlled_buffer_9
  assign ALUOP = or_4_out ? 4'b1011 : 4'bz;  // Controlled_Buffer controlled_buffer_10
  or or_4 (or_4_out, slt, blez, slti);
  assign ALUOP = or_5_out ? 4'b1100 : 4'bz;  // Controlled_Buffer controlled_buffer_11
  or or_5 (or_5_out, sltu, sltiu);
  assign ALUOP = or_6_out ? 4'b0000 : 4'bz;  // Controlled_Buffer controlled_buffer_12
  or or_6 (or_6_out, beq, j, bne, sys, \return , JAL);
  or or_7 (jump, j, JAL);
  or or_8 (RegDst, sltiu, addiu, andi, addi, RegDin, ori, slti);
  or or_9 (AluB, sll, addi, sltiu, addiu, RegDin, andi, ori, sw, slti, SB, sra, srl);
  or or_10 (shift[0], sll, srl, sra);
  not not_1 (not_1_out, or_11_out);
  or or_11 (or_11_out, \return , sys);
  and and_14 (and_14_out, not_1_out, r);
  or or_12 (RegWrite, addi, and_14_out, addiu, sltiu, JAL, andi, RegDin, ori, slti);
  or or_13 (DMWrite, sw, SB);
  or or_14 (inst1, sub, add, beq, addu, bne, \and , slt, SB, sys, \or , blez, \nor , sltiu, sw, \xor );
  or or_15 (inst2, slti, addi, addiu, sltiu, andi, RegDin, ori, \return );
  or or_16 (inst3, sll, srl, sra);
  assign mode = or_17_out ? 4'b1111 : 4'bz;  // Controlled_Buffer controlled_buffer_13
  or or_17 (or_17_out, sw, RegDin);
  assign mode = nor_1_out ? 4'b0000 : 4'bz;  // Controlled_Buffer controlled_buffer_14
  nor nor_1 (nor_1_out, RegDin, sw);
  or or_18 (RS_R, inst1, inst2);
  or or_19 (RT_R, inst1, inst3);

  assign shift[1] = 1'b0;

  // Other names for the same wires on the sheet: AluB_1 = AluB; jr = \return ; lw = RegDin; RegDin1 = RegDin;
  //   RegDst1 = RegDst; syscall = sys
endmodule

module \数据存储器  (
  input  [11:0] \字节地址 ,
  input  [31:0] Din,
  input  CLK,
  input  WE,
  input  [1:0] Mode,
  input  clr,
  output [31:0] DataOut
);

  wire and_1_out, and_2_out, and_3_out, and_4_out, and_5_out, and_6_out, and_7_out, and_8_out, and_9_out,
       and_10_out, and_11_out, and_12_out, and_13_out, and_14_out, buffer_1_out, buffer_2_out, buffer_7_out,
       buffer_8_out, buffer_9_out, buffer_10_out, buffer_11_out, CS0, CS1, CS2, CS3, decoder_1_out3,
       not_2_out, not_3_out, nWE, xor_1_out, \半字访问 , \字节访问 , \字访问 ;
  wire [7:0] buffer_3_out, D0, D1, D2, D3, DIN0, DIN1, DIN2, DIN3;
  wire [15:0] buffer_12_out;
  wire [31:0] bit_extender_1_out, bit_extender_2_out, buffer_14_out, demultiplexer_1_out0,
       demultiplexer_1_out1, demultiplexer_1_out2, demultiplexer_1_out3;

  not not_1 (nWE, WE);
  and and_1 (and_1_out, WE, CS3);
  and and_2 (and_2_out, WE, CS2);
  and and_3 (and_3_out, WE, CS1);
  and and_4 (and_4_out, WE, CS0);
  RAM #(.addrWidth(10), .bus("separate")) ram_1 (
    .addr(\字节地址 [11:2]), .din(DIN3), .data(D3), .str(and_1_out), .clk(CLK), .ld(and_5_out), .clr(clr));  // open: sel
  and and_5 (and_5_out, CS3, nWE);
  RAM #(.addrWidth(10), .bus("separate")) ram_2 (
    .addr(\字节地址 [11:2]), .din(DIN2), .data(D2), .str(and_2_out), .clk(CLK), .ld(and_6_out), .clr(clr));  // open: sel
  and and_6 (and_6_out, CS2, nWE);
  RAM #(.addrWidth(10), .bus("separate")) ram_3 (
    .addr(\字节地址 [11:2]), .din(DIN1), .data(D1), .str(and_3_out), .clk(CLK), .ld(and_7_out), .clr(clr));  // open: sel
  and and_7 (and_7_out, CS1, nWE);
  RAM #(.addrWidth(10), .bus("separate")) ram_4 (
    .addr(\字节地址 [11:2]), .din(DIN0), .data(D0), .str(and_4_out), .clk(CLK), .ld(and_8_out), .clr(clr));  // open: sel
  and and_8 (and_8_out, CS0, nWE);
  buf buffer_1 (buffer_1_out, \字访问 );
  buf buffer_2 (buffer_2_out, \字节访问 );
  assign buffer_3_out = D0;  // Buffer buffer_3, 8 bits wide
  assign buffer_3_out = D1;  // Buffer buffer_4, 8 bits wide
  assign buffer_3_out = D2;  // Buffer buffer_5, 8 bits wide
  assign buffer_3_out = D3;  // Buffer buffer_6, 8 bits wide
  Demultiplexer #(.select(2), .width(32), .enable("false")) demultiplexer_1 (
    .out0(demultiplexer_1_out0), .out1(demultiplexer_1_out1), .out2(demultiplexer_1_out2),
    .out3(demultiplexer_1_out3), .in(Din), .sel(Mode));
  // Probe on DataOut
  buf buffer_7 (buffer_7_out, buffer_1_out);
  and and_9 (and_9_out, \字节地址 [1], \半字访问 );
  buf buffer_8 (buffer_8_out, and_9_out);
  buf buffer_9 (buffer_9_out, \半字访问 );
  xor xor_1 (xor_1_out, \半字访问 , \字节地址 [1]);
  not not_2 (not_2_out, \字节地址 [0]);
  buf buffer_10 (buffer_10_out, \字节地址 [0]);
  buf buffer_11 (buffer_11_out, \字节地址 [1]);
  not not_3 (not_3_out, \字节地址 [1]);
  assign buffer_12_out = {D1, D0};  // Buffer buffer_12, 16 bits wide
  assign buffer_12_out = {D3, D2};  // Buffer buffer_13, 16 bits wide
  and and_10 (and_10_out, buffer_9_out, xor_1_out);
  assign buffer_14_out = {D3, D2, D1, D0};  // Buffer buffer_14, 32 bits wide
  assign bit_extender_1_out = {{24{1'b0}}, buffer_3_out};  // Bit_Extender bit_extender_1
  Multiplexer #(.select(2), .width(32), .enable("false")) multiplexer_1 (
    .in0(buffer_14_out), .in1(bit_extender_1_out), .in2(bit_extender_2_out), .in3({32{1'b0}}), .out(DataOut),
    .sel(Mode));
  assign bit_extender_2_out = {{16{1'b0}}, buffer_12_out};  // Bit_Extender bit_extender_2
  assign DIN0 = demultiplexer_1_out0[7:0] | demultiplexer_1_out1[7:0] | demultiplexer_1_out2[7:0];  // OR_Gate or_1, 8 bits wide
  assign DIN1 = demultiplexer_1_out0[15:8] | demultiplexer_1_out1[7:0] | demultiplexer_1_out2[15:8];  // OR_Gate or_2, 8 bits wide
  assign DIN2 = demultiplexer_1_out0[23:16] | demultiplexer_1_out1[7:0] | demultiplexer_1_out2[7:0];  // OR_Gate or_3, 8 bits wide
  assign DIN3 = demultiplexer_1_out0[31:24] | demultiplexer_1_out1[7:0] | demultiplexer_1_out2[15:8];  // OR_Gate or_4, 8 bits wide
  Decoder #(.select(2), .enable("false")) decoder_1 (
    .out0(\字访问 ), .out1(\字节访问 ), .out2(\半字访问 ), .out3(decoder_1_out3), .sel(Mode));
  and and_11 (and_11_out, buffer_2_out, buffer_10_out, buffer_11_out);
  and and_12 (and_12_out, buffer_2_out, not_2_out, buffer_11_out);
  and and_13 (and_13_out, buffer_2_out, buffer_10_out, not_3_out);
  and and_14 (and_14_out, not_2_out, not_3_out, buffer_2_out);
  or or_5 (CS3, buffer_7_out, buffer_8_out, and_11_out);
  or or_6 (CS2, buffer_7_out, buffer_8_out, and_12_out);
  or or_7 (CS1, buffer_7_out, and_10_out, and_13_out);
  or or_8 (CS0, buffer_7_out, and_10_out, and_14_out);

  // Other names for the same wires on the sheet: Dout[31:0] = DataOut; 字节选择[1:0] = \字节地址 [1:0]; 半字选择 = \字节地址 [1];
  //   字地址[9:0] = \字节地址 [11:2]

  // Notes on the sheet:
  //   输入引脚区
  //   请勿增改引脚，请勿修改子电路封装
  //   电路功能：利用下图中给定的RAM器件实现既既可以按照字节，也可以按照半字，也可以按照32位字访问的MIPS存储器
  //   请在下方利用上方输入输出引脚的隧道信号构建电路，ctrl+d复制选择部件
  //   输出引脚区
endmodule

module NPC (
  input  [31:0] pc_4,
  input  [25:0] imm26,
  input  [31:0] _16_32,
  input  [31:0] reg1,
  input  [31:0] PC4,
  input  jump,
  input  branch,
  input  \return ,
  output [31:0] pcout
);

  wire [31:0] adder_1_out, multiplexer_2_out, multiplexer_3_out, shifter_1_out;

  Shifter #(.width(32)) shifter_1 (.in(_16_32), .\dist (5'b00010), .out(shifter_1_out));
  Multiplexer #(.width(32), .enable("false")) multiplexer_1 (
    .in0(multiplexer_2_out), .in1(reg1), .out(pcout), .sel(\return ));
  Adder #(.width(32)) adder_1 (.a(PC4), .b(shifter_1_out), .out(adder_1_out));  // open: cin, cout
  Multiplexer #(.width(32), .enable("false")) multiplexer_2 (
    .in0(multiplexer_3_out), .in1({pc_4[31:28], imm26, 2'b00}), .out(multiplexer_2_out), .sel(jump));
  Multiplexer #(.width(32), .enable("false")) multiplexer_3 (
    .in0(pc_4), .in1(adder_1_out), .out(multiplexer_3_out), .sel(branch));

  // Other names for the same wires on the sheet: pc4_EX[31:0] = PC4
endmodule

module branch (
  input  beq,
  input  equ,
  input  bne,
  input  blez,
  input  c,
  output branch
);

  wire and_1_out, and_2_out, and_3_out, and_4_out, and_5_out, and_6_out, and_7_out, and_8_out, and_9_out,
       bat, beq_t, blez_t, bne_t, branch_t, buffer_1_out, buffer_2_out, buffer_3_out, buffer_4_out,
       comparator_1_eq, comparator_2_eq, halt, not_1_out, not_2_out, not_3_out, or_1_out, or_2_out, or_5_out,
       syscall, tunnel;
  wire [31:0] alur;

  not not_1 (not_1_out, equ);
  or or_1 (or_1_out, equ, c);
  Comparator #(.width(32)) comparator_1 (.a(32'h1), .b(alur), .eq(comparator_1_eq));  // open: gt, lt
  and and_1 (and_1_out, beq, equ);
  and and_2 (and_2_out, bne, not_1_out);
  and and_3 (and_3_out, blez, or_1_out);
  not not_2 (not_2_out, tunnel);
  or or_2 (or_2_out, tunnel, comparator_1_eq);
  or or_3 (branch, and_1_out, and_2_out, and_3_out);
  and and_4 (and_4_out, beq_t, tunnel);
  and and_5 (and_5_out, bne_t, not_2_out);
  and and_6 (and_6_out, blez_t, or_2_out);
  or or_4 (branch_t, and_4_out, and_5_out, and_6_out);
  buf buffer_1 (buffer_1_out, beq_t);
  and and_7 (and_7_out, buffer_1_out, buffer_2_out);
  buf buffer_2 (buffer_2_out, tunnel);
  not not_3 (not_3_out, tunnel);
  and and_8 (and_8_out, not_3_out, buffer_3_out);
  buf buffer_3 (buffer_3_out, bne_t);
  buf buffer_4 (buffer_4_out, blez_t);
  and and_9 (and_9_out, buffer_4_out, or_5_out);
  or or_5 (or_5_out, tunnel, comparator_2_eq);
  Comparator #(.width(32)) comparator_2 (.a(32'h1), .b(alur), .eq(comparator_2_eq));  // open: gt, lt
  or or_6 (branch_t, and_7_out, and_8_out, and_9_out);
  nand nand_1 (halt, syscall, tunnel);
  or or_7 (bat, beq_t, blez_t, bne_t);
endmodule

module \计数器  (
  input  clk,
  input  branch,
  input  jump,
  input  RST,
  input  bat,
  input  \return ,
  input  pop,
  input  halt,
  output [15:0] \总周期 ,
  output [15:0] \无条件 ,
  output [15:0] \有条件 ,
  output [15:0] \有条件成功 ,
  output [15:0] pop_2
);

  wire or_1_out, or_2_out, register_1_q;

  Counter #(.width(16), .max('hffff)) counter_1 (.count(bat), .Q(\有条件 ), .clk(clk), .clr(RST));  // open: load, D, carry
  Counter #(.width(16), .max('hffff)) counter_2 (
    .count(or_1_out), .Q(\无条件 ), .clk(clk), .clr(RST));  // open: load, D, carry
  or or_1 (or_1_out, jump, \return );
  Register #(.width(1)) register_1 (.D(halt), .Q(register_1_q), .clk(clk));  // open: en, clr
  Counter #(.width(16), .max('hffff)) counter_3 (
    .count(or_2_out), .Q(\总周期 ), .clk(clk), .clr(RST));  // open: load, D, carry
  or or_2 (or_2_out, halt, register_1_q);
  Counter #(.width(16), .max('hffff)) counter_4 (
    .count(branch), .Q(\有条件成功 ), .clk(clk), .clr(RST));  // open: load, D, carry
  Counter #(.width(16), .max('hffff)) counter_5 (.count(pop), .Q(pop_2), .clk(clk), .clr(RST));  // open: load, D, carry

  // Other names for the same wires on the sheet: pop_out[15:0] = pop_2; 总周期数[15:0] = \总周期 ; 无条件分支指令数[15:0] = \无条件 ;
  //   有条件分支成功跳转[15:0] = \有条件成功 ; 有条件分支指令数[15:0] = \有条件 
endmodule

module \显示器  (
  input  sys,
  input  clk,
  input  in_3,
  input  rst,
  input  [31:0] reg2,
  output [31:0] syscallout
);

  wire and_1_out, not_1_out;

  not not_1 (not_1_out, in_3);
  Register #(.width(32)) register_1 (.D(reg2), .en(and_1_out), .Q(syscallout), .clk(clk), .clr(rst));
  and and_1 (and_1_out, sys, not_1_out);

  // Other names for the same wires on the sheet: syscall = sys; tunnel = in_3
endmodule

module \程序计数器  (
  input  clk,
  input  rst,
  input  halt,
  input  [31:0] pcout,
  output [31:0] pc4,
  output [9:0] pc_instru
);

  wire [31:0] PC_q;

  Register #(.width(32)) PC (.D(pcout), .en(halt), .Q({PC_q[31:12], pc_instru, PC_q[1:0]}), .clk(clk), .clr(rst));
  Adder #(.width(32)) adder_1 (.a({PC_q[31:12], pc_instru, PC_q[1:0]}), .b(32'h4), .out(pc4));  // open: cin, cout
endmodule

module \IF_ID锁存  (
  input  [31:0] \指令 ,
  input  [31:0] pc4,
  input  clk,
  input  rst,
  input  halt,
  output [31:0] \输出指令 ,
  output [31:0] pc_4
);

  wire [31:0] and_1_out, and_2_out;
  wire [31:31] not_1_out;

  assign and_1_out = pc4 & {32{not_1_out[31]}};  // AND_Gate and_1, 32 bits wide
  assign and_2_out = \指令  & {32{not_1_out[31]}};  // AND_Gate and_2, 32 bits wide
  not not_1 (not_1_out[31], rst);
  Register #(.width(32)) u_pc4 (.D(and_1_out), .en(halt), .Q(pc_4), .clk(clk));  // open: clr
  Register #(.width(32)) IR (.D(and_2_out), .en(halt), .Q(\输出指令 ), .clk(clk));  // open: clr

  // Other names for the same wires on the sheet: instru[31:0] = \指令 ; IR[31:0] = \输出指令 
endmodule

module \指令解析器IR  (
  input  [31:0] \输入指令 ,
  input  [1:0] shift,
  output [5:0] op,
  output [5:0] func,
  output [31:0] ins16_32,
  output [4:0] rs,
  output [4:0] rt,
  output [4:0] rd,
  output [25:0] ins26,
  output [31:0] ins
);

  wire [31:0] bit_extender_2_out;

  assign ins16_32 = {{16{\输入指令 [15]}}, \输入指令 [15:0]};  // Bit_Extender bit_extender_1
  assign bit_extender_2_out = {{27{1'b0}}, \输入指令 [10:6]};  // Bit_Extender bit_extender_2
  Multiplexer #(.select(2), .width(32), .enable("false")) multiplexer_1 (
    .in0(ins16_32), .in1(bit_extender_2_out), .in2(ins16_32), .out(ins), .sel(shift));  // open: in3

  assign func = \输入指令 [5:0];
  assign ins26 = \输入指令 [25:0];
  assign op = \输入指令 [31:26];
  assign rd = \输入指令 [15:11];
  assign rs = \输入指令 [25:21];
  assign rt = \输入指令 [20:16];

  // Other names for the same wires on the sheet: ins16[15:0] = \输入指令 [15:0]; 输入[31:0] = \输入指令 ;
  //   shamt[4:0] = \输入指令 [10:6]
endmodule

module \寄存器文件  (
  input  jal,
  input  syscall,
  input  [4:0] rs,
  input  [31:0] aluR,
  input  [4:0] rt,
  input  RegDst,
  input  [4:0] rd,
  input  RegWrite,
  input  [31:0] DMout,
  input  RegDin,
  input  clk,
  input  [31:0] pc4,
  output [31:0] A,
  output [31:0] B
);

  wire [4:0] multiplexer_3_out, multiplexer_4_out, multiplexer_5_out, registerfile_1_p6;
  wire [31:0] multiplexer_1_out, multiplexer_2_out;

  Multiplexer #(.width(32), .enable("false")) multiplexer_1 (
    .in0(aluR), .in1(DMout), .out(multiplexer_1_out), .sel(RegDin));
  Multiplexer #(.width(32), .enable("false")) multiplexer_2 (
    .in0(multiplexer_1_out), .in1(pc4), .out(multiplexer_2_out), .sel(jal));
  Multiplexer #(.width(5), .enable("false")) multiplexer_3 (
    .in0(multiplexer_4_out), .in1({5{1'b1}}), .out(multiplexer_3_out), .sel(jal));
  Multiplexer #(.width(5), .enable("false")) multiplexer_4 (.in0(rs), .in1(rt), .out(multiplexer_4_out), .sel(RegDst));
  Multiplexer #(.width(5), .enable("false")) multiplexer_5 (
    .in0(rd), .in1(5'b00010), .out(multiplexer_5_out), .sel(syscall));
  // RegisterFile registerfile_1: pin names not known; wires that end beside it: multiplexer_2_out, clk, RegWrite, multiplexer_3_out, multiplexer_5_out, registerfile_1_p6, A, B
  Multiplexer #(.width(5), .enable("false")) multiplexer_6 (
    .in0(rt), .in1(5'b00100), .out(registerfile_1_p6), .sel(syscall));
endmodule

module \运算器ALU  (
  input  [31:0] reg1,
  input  shift,
  input  syscall,
  input  [3:0] aluop,
  input  [31:0] reg2,
  input  [31:0] ins,
  output [31:0] aluR,
  output equal
);

  wire AluB_1;
  wire [31:0] alu_1_p2, multiplexer_1_out, multiplexer_2_out;

  Multiplexer #(.width(32), .enable("false")) multiplexer_1 (
    .in0(reg2), .in1(ins), .out(multiplexer_1_out), .sel(AluB_1));
  Multiplexer #(.width(32), .enable("false")) multiplexer_2 (
    .in0(reg1), .in1(reg2), .out(multiplexer_2_out), .sel(shift));
  // ALU alu_1: pin names not known; wires that end beside it: multiplexer_2_out, alu_1_p2, aluop, equal, aluR
  Multiplexer #(.width(32), .enable("false")) multiplexer_3 (
    .in0(multiplexer_1_out), .in1(32'ha), .out(alu_1_p2), .sel(syscall));
endmodule

module ID_EX (
  input  [31:0] reg1,
  input  [31:0] reg2,
  input  [31:0] ins,
  input  [31:0] pc4,
  input  [21:0] ctrl,
  input  clk,
  input  [4:0] rs,
  input  [4:0] rd,
  input  [4:0] rt,
  input  halt,
  input  [25:0] ins26,
  input  [31:0] ins16_32,
  input  Bub_Signal,
  input  Rt_R,
  input  RS_R,
  output [31:0] reg_1,
  output [31:0] reg_2,
  output [31:0] instant,
  output [31:0] pc_4,
  output [21:0] ctrl_,
  output [4:0] rs_,
  output [4:0] rd_,
  output [31:0] ins16_32_,
  output [25:0] ins26_2,
  output RT_R_,
  output RS_R_,
  output [4:0] rt_
);

  wire and_1_out, and_2_out;
  wire [4:0] and_3_out, and_4_out, and_5_out;
  wire [4:4] not_1_out;
  wire [21:0] and_6_out;
  wire [25:0] and_7_out;
  wire [31:0] and_8_out, and_9_out, and_10_out, and_11_out, and_12_out;

  and and_1 (and_1_out, RS_R, not_1_out[4]);
  and and_2 (and_2_out, Rt_R, not_1_out[4]);
  assign and_3_out = rd & {5{not_1_out[4]}};  // AND_Gate and_3, 5 bits wide
  assign and_4_out = rs & {5{not_1_out[4]}};  // AND_Gate and_4, 5 bits wide
  assign and_5_out = rt & {5{not_1_out[4]}};  // AND_Gate and_5, 5 bits wide
  assign and_6_out = ctrl & {22{not_1_out[4]}};  // AND_Gate and_6, 22 bits wide
  assign and_7_out = ins26 & {26{not_1_out[4]}};  // AND_Gate and_7, 26 bits wide
  assign and_8_out = pc4 & {32{not_1_out[4]}};  // AND_Gate and_8, 32 bits wide
  assign and_9_out = reg1 & {32{not_1_out[4]}};  // AND_Gate and_9, 32 bits wide
  assign and_10_out = reg2 & {32{not_1_out[4]}};  // AND_Gate and_10, 32 bits wide
  assign and_11_out = ins & {32{not_1_out[4]}};  // AND_Gate and_11, 32 bits wide
  assign and_12_out = ins16_32 & {32{not_1_out[4]}};  // AND_Gate and_12, 32 bits wide
  not not_1 (not_1_out[4], Bub_Signal);
  Register #(.width(1)) u_rs (.D(and_1_out), .en(halt), .Q(RS_R_), .clk(clk), .clr(1'b0));
  Register #(.width(1)) rs_2 (.D(and_2_out), .en(halt), .Q(RT_R_), .clk(clk), .clr(1'b0));
  Register #(.width(5)) rs_3 (.D(and_3_out), .en(halt), .Q(rd_), .clk(clk), .clr(1'b0));
  Register #(.width(5)) rs_4 (.D(and_4_out), .en(halt), .Q(rs_), .clk(clk), .clr(1'b0));
  Register #(.width(5)) u_rt (.D(and_5_out), .en(halt), .Q(rt_), .clk(clk), .clr(1'b0));
  Register #(.width(22)) u_ctrl (.D(and_6_out), .en(halt), .Q(ctrl_), .clk(clk), .clr(1'b0));
  Register #(.width(26)) ctrl_2 (.D(and_7_out), .en(halt), .Q(ins26_2), .clk(clk), .clr(1'b0));
  Register #(.width(32)) IR (.D(and_8_out), .en(halt), .Q(pc_4), .clk(clk), .clr(1'b0));
  Register #(.width(32)) IR_2 (.D(and_9_out), .en(halt), .Q(reg_1), .clk(clk), .clr(1'b0));
  Register #(.width(32)) IR_3 (.D(and_10_out), .en(halt), .Q(reg_2), .clk(clk), .clr(1'b0));
  Register #(.width(32)) IR_4 (.D(and_11_out), .en(halt), .Q(instant), .clk(clk), .clr(1'b0));
  Register #(.width(32)) IR_5 (.D(and_12_out), .en(halt), .Q(ins16_32_), .clk(clk), .clr(1'b0));

  // Other names for the same wires on the sheet: ins26_[25:0] = ins26_2
endmodule

module EX_MEM (
  input  [31:0] aluR,
  input  [31:0] reg2,
  input  [31:0] pc4,
  input  clk,
  input  rst,
  input  [22:0] ctrl,
  input  [4:0] rs,
  input  [4:0] rt,
  input  [4:0] rd,
  input  halt,
  output [31:0] pc_4,
  output [22:0] ctrl_,
  output [4:0] rs_,
  output [4:0] rd_,
  output [4:0] rt_,
  output [31:0] alu_R,
  output [31:0] reg_2
);

  Register #(.width(5)) u_rd (.D(rd), .en(halt), .Q(rd_), .clk(clk), .clr(rst));
  Register #(.width(5)) u_rs (.D(rs), .en(halt), .Q(rs_), .clk(clk), .clr(rst));
  Register #(.width(5)) u_rt (.D(rt), .en(halt), .Q(rt_), .clk(clk), .clr(rst));
  Register #(.width(23)) u_ctrl (.D(ctrl), .en(halt), .Q(ctrl_), .clk(clk), .clr(rst));
  Register #(.width(32)) u_pc4 (.D(pc4), .en(halt), .Q(pc_4), .clk(clk), .clr(rst));
  Register #(.width(32)) IR (.D(reg2), .en(halt), .Q(reg_2), .clk(clk), .clr(rst));
  Register #(.width(32)) IR_2 (.D(aluR), .en(halt), .Q(alu_R), .clk(clk), .clr(rst));
endmodule

module MEM_WB (
  input  [31:0] DMout,
  input  [31:0] pc4,
  input  [31:0] aluR,
  input  clk,
  input  rst,
  input  [22:0] ctrl,
  input  [4:0] rs,
  input  [4:0] rt,
  input  [4:0] rd,
  input  halt,
  output [31:0] DM_out,
  output [22:0] ctrl_,
  output [4:0] rs_,
  output [31:0] pc_4,
  output [4:0] rt_,
  output [31:0] alu_R,
  output [4:0] rd_
);

  Register #(.width(5)) u_rs (.D(rd), .en(halt), .Q(rd_), .clk(clk), .clr(rst));
  Register #(.width(5)) rs_2 (.D(rs), .en(halt), .Q(rs_), .clk(clk), .clr(rst));
  Register #(.width(5)) u_rt (.D(rt), .en(halt), .Q(rt_), .clk(clk), .clr(rst));
  Register #(.width(23)) u_ctrl (.D(ctrl), .en(halt), .Q(ctrl_), .clk(clk), .clr(rst));
  Register #(.width(32)) u_pc4 (.D(pc4), .en(halt), .Q(pc_4), .clk(clk), .clr(rst));
  Register #(.width(32)) u_aluR (.D(aluR), .en(halt), .Q(alu_R), .clk(clk), .clr(rst));
  Register #(.width(32)) IR (.D(DMout), .en(halt), .Q(DM_out), .clk(clk), .clr(rst));
endmodule

module branch_halt (
  input  beq,
  input  bne,
  input  blez,
  input  syscall,
  input  in_5,
  input  [31:0] alur,
  output branch,
  output bat
);

  wire and_1_out, and_2_out, and_3_out, comparator_1_eq, not_1_out, or_1_out;

  or or_1 (or_1_out, in_5, comparator_1_eq);
  Comparator #(.width(32)) comparator_1 (.a(32'h1), .b(alur), .eq(comparator_1_eq));  // open: gt, lt
  not not_1 (not_1_out, in_5);
  and and_1 (and_1_out, beq, in_5);
  and and_2 (and_2_out, bne, not_1_out);
  and and_3 (and_3_out, blez, or_1_out);
  or or_2 (branch, and_1_out, and_2_out, and_3_out);
  or or_3 (bat, beq, blez, bne);

  // Other names for the same wires on the sheet: tunnel = in_5
endmodule

module \气泡检测  (
  input  RT_R,
  input  RS_R,
  input  [4:0] RB,
  input  RegWriteEX,
  input  RegDinEx,
  input  [4:0] RA,
  input  [4:0] RS_EX,
  input  [4:0] RT_EX,
  input  reg_EX,
  input  jal_EX,
  input  J,
  input  Branch,
  input  Ret,
  output Bub_Signal,
  output UN_LoadUseSignal,
  output Jump_RESET
);

  wire and_1_out, and_2_out, comparator_1_eq, comparator_2_eq, comparator_3_eq, not_1_out, not_2_out,
       or_1_out;
  wire [4:0] multiplexer_1_out, multiplexer_2_out;

  Multiplexer #(.width(5), .enable("false")) multiplexer_1 (
    .in0(RS_EX), .in1(RT_EX), .out(multiplexer_1_out), .sel(reg_EX));
  Multiplexer #(.width(5), .enable("false")) multiplexer_2 (
    .in0(multiplexer_1_out), .in1({5{1'b1}}), .out(multiplexer_2_out), .sel(jal_EX));
  Comparator #(.width(5)) comparator_1 (.a(multiplexer_2_out), .b({5{1'b0}}), .eq(comparator_1_eq));  // open: gt, lt
  Comparator #(.width(5)) comparator_2 (.a(multiplexer_2_out), .b(RA), .eq(comparator_2_eq));  // open: gt, lt
  not not_1 (not_1_out, comparator_1_eq);
  Comparator #(.width(5)) comparator_3 (.a(multiplexer_2_out), .b(RB), .eq(comparator_3_eq));  // open: gt, lt
  and and_1 (and_1_out, comparator_2_eq, RS_R, not_1_out);
  and and_2 (and_2_out, not_1_out, RT_R, comparator_3_eq);
  or or_1 (or_1_out, and_1_out, and_2_out);
  not not_2 (not_2_out, RegDinEx);
  and and_3 (Bub_Signal, or_1_out, RegWriteEX, RegDinEx);
  and and_4 (UN_LoadUseSignal, or_1_out, not_2_out);
  or or_2 (Jump_RESET, J, Branch, Ret);
endmodule

module \重定向  (
  input  [4:0] RS_EX,
  input  rs_r,
  input  [4:0] RT_EX,
  input  rt_r,
  input  [4:0] rw4,
  input  [4:0] rw5,
  input  regWrite4,
  input  Sys_EX,
  input  regWrite5,
  input  RegDin4,
  input  jal4,
  output sel1,
  output sel2,
  output sel3,
  output sel4
);

  wire comparator_1_eq, comparator_2_eq, comparator_3_eq, comparator_4_eq, comparator_5_eq, not_1_out,
       not_2_out, not_3_out;
  wire [4:0] ra, rb;

  Comparator #(.width(5)) comparator_1 (.a(rw4), .b(ra), .eq(comparator_1_eq));  // open: gt, lt
  Comparator #(.width(5)) comparator_2 (.a(rw4), .b({5{1'b0}}), .eq(comparator_2_eq));  // open: gt, lt
  Comparator #(.width(5)) comparator_3 (.a(rw4), .b(rb), .eq(comparator_3_eq));  // open: gt, lt
  not not_1 (not_1_out, comparator_2_eq);
  not not_2 (not_2_out, RegDin4);
  not not_3 (not_3_out, jal4);
  and and_1 (sel1, rs_r, comparator_1_eq, not_1_out, not_2_out, not_3_out, regWrite4);
  and and_2 (sel2, not_2_out, not_1_out, not_3_out, regWrite4, rt_r, comparator_3_eq);
  Comparator #(.width(5)) comparator_4 (.a(rw5), .b(ra), .eq(comparator_4_eq));  // open: gt, lt
  Comparator #(.width(5)) comparator_5 (.a(rw5), .b(rb), .eq(comparator_5_eq));  // open: gt, lt
  and and_3 (sel3, rs_r, comparator_4_eq, regWrite5);
  and and_4 (sel4, rt_r, comparator_5_eq, regWrite5);
  Multiplexer #(.width(5), .enable("false")) multiplexer_1 (.in0(RS_EX), .in1(5'b00010), .out(ra), .sel(Sys_EX));
  Multiplexer #(.width(5), .enable("false")) multiplexer_2 (.in0(RT_EX), .in1(5'b00100), .out(rb), .sel(Sys_EX));

  // Other names for the same wires on the sheet: RS[4:0] = RS_EX; RT[4:0] = RT_EX
endmodule
